// Logisim project 4bit_bcd_adder.circ as structural Verilog: 1 circuit, main circuit main
module main (
  input  A4,
  input  A3,
  input  A2,
  input  A1,
  input  in_5,
  input  B4,
  input  B3,
  input  B2,
  input  B1,
  output C4,
  output I4,
  output I3,
  output I2,
  output I1
);

  _74283 u_74283_1 (
    .pin1(I2), .pin2(B2), .pin3(A2), .pin4(I1), .pin5(A1), .pin6(B1), .pin7(in_5), .pin15(B3), .pin14(A3),
    .pin13(I3), .pin12(A4), .pin11(B4), .pin10(I4), .pin9(C4));

  // Notes on the sheet:
  //   4 Bit BCD adder
endmodule
