// Logisim project Binary_Counter.circ as structural Verilog: 1 circuit, main circuit main
module main (
  input  in_1,
  input  UP,
  input  in_3,
  output out_4,
  output out_5,
  output out_6,
  output out_7,
  output out_8,
  output out_9,
  output out_10,
  output out_11
);

  wire and_1_out, and_2_out, and_3_out, and_4_out, and_5_out, and_6_out, clock_1_out, clock_2_out,
       clock_3_out, d_ff_4_qn, or_1_out, or_2_out, or_3_out, or_4_out, t_ff_2_q, t_ff_2_qn, t_ff_4_q,
       t_ff_7_q, t_ff_8_q;

  Clock clock_1 (.out(clock_1_out));
  Clock clock_2 (.out(clock_2_out));
  or or_1 (or_1_out, UP, in_3);
  Clock clock_3 (.out(clock_3_out));
  D_Flip_Flop #(.trigger("falling")) d_ff_1 (.D(d_ff_4_qn), .clk(clock_2_out), .Q(out_11));  // open: Qn, preset, reset
  T_Flip_Flop #(.trigger("falling")) t_ff_1 (.T(in_1), .clk(clock_1_out), .Q(out_7));  // open: Qn, reset, preset
  T_Flip_Flop t_ff_2 (.T(or_1_out), .clk(clock_3_out), .Q(t_ff_2_q), .Qn(t_ff_2_qn));  // open: reset, preset
  and and_1 (and_1_out, in_1, out_7);
  T_Flip_Flop #(.trigger("falling")) t_ff_3 (.T(and_1_out), .clk(clock_1_out), .Q(out_6));  // open: Qn, reset, preset
  and and_2 (and_2_out, UP, t_ff_2_q);
  T_Flip_Flop t_ff_4 (.T(or_2_out), .clk(clock_3_out), .Q(t_ff_4_q));  // open: Qn, reset, preset
  or or_2 (or_2_out, and_2_out, UP);
  D_Flip_Flop #(.trigger("falling")) d_ff_2 (.D(out_11), .clk(clock_2_out), .Q(out_10));  // open: Qn, preset, reset
  and and_3 (and_3_out, and_1_out, out_6);
  T_Flip_Flop #(.trigger("falling")) t_ff_5 (.T(and_3_out), .clk(clock_1_out), .Q(out_5));  // open: Qn, reset, preset
  and and_4 (and_4_out, t_ff_4_q, and_2_out);
  or or_3 (or_3_out, and_4_out, and_2_out);
  D_Flip_Flop #(.trigger("falling")) d_ff_3 (.D(out_10), .clk(clock_2_out), .Q(out_9));  // open: Qn, preset, reset
  and and_5 (and_5_out, and_3_out, out_5);
  T_Flip_Flop #(.trigger("falling")) t_ff_6 (.T(and_5_out), .clk(clock_1_out), .Q(out_4));  // open: Qn, reset, preset
  T_Flip_Flop t_ff_7 (.T(or_3_out), .clk(clock_3_out), .Q(t_ff_7_q));  // open: Qn, reset, preset
  and and_6 (and_6_out, t_ff_7_q, and_4_out);
  D_Flip_Flop #(.trigger("falling")) d_ff_4 (
    .D(out_9), .clk(clock_2_out), .Q(out_8), .Qn(d_ff_4_qn));  // open: preset, reset
  T_Flip_Flop t_ff_8 (.T(or_4_out), .clk(clock_3_out), .Q(t_ff_8_q));  // open: Qn, reset, preset
  or or_4 (or_4_out, and_6_out, and_4_out);

  // Notes on the sheet:
  //   Johnson Counter(Synchronous Counter)
  //   Binary Up-Down Counter(Synchrous Counter) incomplete
  //   Binary Up Counter(Synchronous)
endmodule
