// Logisim project HalfAdder.circ as structural Verilog: 1 circuit, main circuit main
module main (
  input  x,
  input  y,
  input  z
);

  wire and_1_out, and_2_out, or_1_out, xor_1_out, xor_2_out;

  xor xor_1 (xor_1_out, x, y);
  and and_1 (and_1_out, x, y);
  xor xor_2 (xor_2_out, xor_1_out, z);
  and and_2 (and_2_out, xor_1_out, z);
  LED led_1 (.in(xor_2_out));
  or or_1 (or_1_out, and_2_out, and_1_out);
  LED led_2 (.in(or_1_out));

  // Notes on the sheet:
  //   Full Adder
endmodule
