// Logisim project MUX_DMUX(4 1).circ as structural Verilog: 1 circuit, main circuit main
module main (
  input  I0,
  input  I1,
  input  I2,
  input  I3,
  input  [1:0] s1s0,
  input  a,
  input  b,
  input  c,
  input  d,
  input  S1,
  input  S0,
  input  p,
  input  q,
  input  r,
  input  s,
  input  z,
  input  y
);

  wire and_1_out, and_2_out, and_3_out, and_4_out, and_5_out, and_6_out, and_7_out, and_8_out,
       demultiplexer_1_out0, demultiplexer_1_out1, demultiplexer_1_out2, demultiplexer_1_out3,
       multiplexer_1_out, n7411_1_pin2, n7411_1_pin6, n7411_1_pin8, n7411_1_pin12, n7411_2_pin12,
       n7411_3_pin6, n7411_3_pin8, n7411_3_pin12, n7411_4_pin12, n7432_1_pin3, n7432_1_pin8, n7432_1_pin11,
       n7432_2_pin3, n7432_2_pin8, n7432_2_pin11, not_1_out, not_2_out, not_3_out, or_1_out;

  Multiplexer #(.select(2)) multiplexer_1 (.in0(I0), .in1(I1), .in2(I2), .in3(I3), .out(multiplexer_1_out), .sel(s1s0));
  not not_1 (not_1_out, S1);
  not not_2 (not_2_out, S0);
  not not_3 (not_3_out, y);
  Demultiplexer #(.select(2)) demultiplexer_1 (
    .out0(demultiplexer_1_out0), .out1(demultiplexer_1_out1), .out2(demultiplexer_1_out2),
    .out3(demultiplexer_1_out3), .in(multiplexer_1_out), .sel(s1s0));
  and and_1 (and_1_out, a, not_1_out, not_2_out);
  and and_2 (and_2_out, b, S0, not_1_out);
  and and_3 (and_3_out, c, S1, not_2_out);
  and and_4 (and_4_out, d, S0, S1);
  _7411 u_7411_1 (
    .pin1(p), .pin2(n7411_1_pin2), .pin3(r), .pin4(z), .pin5(not_3_out), .pin6(n7411_1_pin6),
    .pin13(not_3_out), .pin12(n7411_1_pin12), .pin11(n7411_1_pin2), .pin10(y), .pin9(q), .pin8(n7411_1_pin8));
  not not_4 (n7411_1_pin2, z);
  LED led_1 (.in(demultiplexer_1_out0));
  LED led_2 (.in(demultiplexer_1_out1));
  LED led_3 (.in(demultiplexer_1_out2));
  LED led_4 (.in(demultiplexer_1_out3));
  or or_1 (or_1_out, and_1_out, and_2_out, and_3_out, and_4_out);
  _7411 u_7411_2 (
    .pin1(s), .pin2(z), .pin13(y), .pin12(n7411_2_pin12));  // open: pin3, pin4, pin5, pin6, pin11, pin10, pin9, pin8
  _7432 u_7432_1 (
    .pin1(n7411_2_pin12), .pin2(n7411_1_pin6), .pin3(n7432_1_pin3), .pin13(n7411_1_pin12),
    .pin12(n7411_1_pin8), .pin11(n7432_1_pin11), .pin10(n7432_1_pin11), .pin9(n7432_1_pin3),
    .pin8(n7432_1_pin8));  // open: pin4, pin5, pin6
  _7411 u_7411_3 (
    .pin1(n7411_1_pin2), .pin2(not_3_out), .pin3(n7411_1_pin2), .pin4(y), .pin5(n7432_1_pin8),
    .pin6(n7411_3_pin6), .pin13(n7432_1_pin8), .pin12(n7411_3_pin12), .pin11(z), .pin10(not_3_out),
    .pin9(n7432_1_pin8), .pin8(n7411_3_pin8));
  and and_5 (and_5_out, not_1_out, or_1_out, not_2_out);
  and and_6 (and_6_out, S0, or_1_out, not_1_out);
  and and_7 (and_7_out, S1, or_1_out, not_2_out);
  and and_8 (and_8_out, S0, or_1_out, S1);
  LED D0 (.in(and_5_out));
  LED D1 (.in(and_6_out));
  LED D2 (.in(and_7_out));
  LED D3 (.in(and_8_out));
  _7411 u_7411_4 (
    .pin1(z), .pin2(y), .pin13(n7432_1_pin8), .pin12(n7411_4_pin12));  // open: pin3, pin4, pin5, pin6, pin11, pin10, pin9, pin8
  _7432 u_7432_2 (
    .pin1(n7411_3_pin8), .pin2(n7411_3_pin12), .pin3(n7432_2_pin3), .pin13(n7411_4_pin12),
    .pin12(n7411_3_pin6), .pin11(n7432_2_pin11), .pin10(n7432_2_pin11), .pin9(n7432_2_pin3),
    .pin8(n7432_2_pin8));  // open: pin4, pin5, pin6
  LED led_5 (.in(n7432_1_pin8));
  LED led_6 (.in(n7432_2_pin8));

  // Notes on the sheet:
  //   pz'y'
  //   qyz'
  //   rzy'
  //   szy
  //   z'y'D
  //   z'yD
  //   Dzy'
  //   MUX(D) = pz'y'+ szy + rzy' + szy
  //   Demux = Dy'z' + Dy'z + Dyz' + Dyz
endmodule
