// Logisim project RS_flip_flop.circ as structural Verilog: 1 circuit, main circuit main
module main (
  input  R,
  input  S
);

  wire and_1_out, and_2_out, clock_1_out, nor_1_out, nor_2_out;

  Clock clock_1 (.out(clock_1_out));
  and and_1 (and_1_out, R, clock_1_out);
  and and_2 (and_2_out, clock_1_out, S);
  nor nor_1 (nor_1_out, and_1_out, nor_2_out);
  nor nor_2 (nor_2_out, nor_1_out, and_2_out);
  LED Q (.in(nor_1_out));
  LED Q1 (.in(nor_2_out));

  // Notes on the sheet:
  //   RS Flip Flop
endmodule
