// Logisim project bcd_counter.circ as structural Verilog: 1 circuit, main circuit main
module main (
  input  in_1,
  output out_2,
  output out_3,
  output out_4,
  output out_5
);

  wire and_1_out, B_qn, clock_1_out, D_qn;

  Clock clock_1 (.out(clock_1_out));
  J_K_Flip_Flop #(.trigger("falling")) D (
    .J(in_1), .K(in_1), .clk(clock_1_out), .Q(out_5), .Qn(D_qn), .reset(and_1_out));  // open: preset
  J_K_Flip_Flop #(.trigger("falling")) C (
    .J(in_1), .K(in_1), .clk(out_5), .Q(out_4), .reset(and_1_out));  // open: Qn, preset
  J_K_Flip_Flop #(.trigger("falling")) B (
    .J(in_1), .K(in_1), .clk(out_4), .Q(out_3), .Qn(B_qn), .reset(and_1_out));  // open: preset
  J_K_Flip_Flop #(.trigger("falling")) A (
    .J(in_1), .K(in_1), .clk(out_3), .Q(out_2), .reset(and_1_out));  // open: Qn, preset
  and and_1 (and_1_out, out_2, B_qn, out_4, D_qn);

  // Notes on the sheet:
  //   BCD Counter
endmodule
