// Logisim project decoder_circuit.circ as structural Verilog: 1 circuit, main circuit main
module main (
  input  a,
  input  b,
  input  c,
  output d0,
  output d1,
  output d2,
  output d3,
  output d4,
  output d5,
  output d6,
  output d7
);

  wire not_1_out, not_2_out, not_3_out;

  not not_1 (not_1_out, a);
  not not_2 (not_2_out, b);
  not not_3 (not_3_out, c);
  and and_1 (d0, not_1_out, not_2_out, not_3_out);
  and and_2 (d1, not_1_out, not_2_out, c);
  and and_3 (d2, not_1_out, b, not_3_out);
  and and_4 (d3, not_1_out, b, c);
  and and_5 (d4, a, not_2_out, not_3_out);
  and and_6 (d5, a, not_2_out, c);
  and and_7 (d6, a, b, not_3_out);
  and and_8 (d7, a, b, c);

  // Notes on the sheet:
  //   Decoder
endmodule
