// Logisim project decoder_ic.circ as structural Verilog: 1 circuit, main circuit main
module main (
  input  in_1,
  input  in_2,
  input  in_3,
  input  in_4,
  input  in_5,
  input  in_6
);

  wire n74138_1_pin7, n74138_1_pin9, n74138_1_pin10, n74138_1_pin11, n74138_1_pin12, n74138_1_pin13,
       n74138_1_pin14, n74138_1_pin15;

  LED led_1 (.in(n74138_1_pin15));
  LED led_2 (.in(n74138_1_pin14));
  LED led_3 (.in(n74138_1_pin13));
  _74138 u_74138_1 (
    .pin1(in_3), .pin2(in_2), .pin3(in_1), .pin4(in_4), .pin5(in_5), .pin6(in_6), .pin7(n74138_1_pin7),
    .pin15(n74138_1_pin15), .pin14(n74138_1_pin14), .pin13(n74138_1_pin13), .pin12(n74138_1_pin12),
    .pin11(n74138_1_pin11), .pin10(n74138_1_pin10), .pin9(n74138_1_pin9));
  LED led_4 (.in(n74138_1_pin12));
  LED led_5 (.in(n74138_1_pin11));
  LED led_6 (.in(n74138_1_pin10));
  LED led_7 (.in(n74138_1_pin9));
  LED led_8 (.in(n74138_1_pin7));

  // Notes on the sheet:
  //   Decoder
endmodule
