// Logisim project full_adder_subtractor.circ as structural Verilog: 1 circuit, main circuit main
module main (
  input  x,
  input  y,
  input  z,
  input  in_4,
  input  in_5,
  input  in_6
);

  wire and_1_out, and_2_out, and_3_out, and_4_out, not_1_out, not_2_out, or_1_out, or_2_out, xor_1_out,
       xor_2_out, xor_3_out, xor_4_out;

  xor xor_1 (xor_1_out, x, y);
  and and_1 (and_1_out, x, y);
  not not_1 (not_1_out, in_4);
  xor xor_2 (xor_2_out, in_4, in_5);
  and and_2 (and_2_out, not_1_out, in_5);
  not not_2 (not_2_out, xor_2_out);
  xor xor_3 (xor_3_out, xor_1_out, z);
  and and_3 (and_3_out, xor_1_out, z);
  or or_1 (or_1_out, and_3_out, and_1_out);
  xor xor_4 (xor_4_out, xor_2_out, in_6);
  and and_4 (and_4_out, not_2_out, in_6);
  LED SUM (.in(xor_3_out));
  LED carry (.in(or_1_out));
  LED led_1 (.in(xor_4_out));
  or or_2 (or_2_out, and_2_out, and_4_out);
  LED led_2 (.in(or_2_out));

  // Notes on the sheet:
  //   Full Adder
  //   Full Subtractor
endmodule
