// Logisim project mux_function_implementation.circ as structural Verilog: 1 circuit, main circuit main
module main (
  input  in_1,
  input  in_2,
  input  A,
  input  [1:0] BC,
  input  in_5,
  input  in_6,
  input  in_7,
  input  X,
  input  [2:0] in_9,
  output out_10
);

  wire multiplexer_1_out, multiplexer_2_out, n74157_1_pin3, not_1_out, not_2_out, not_3_out;

  not not_1 (not_1_out, in_7);
  not not_2 (not_2_out, X);
  Multiplexer #(.select(3)) multiplexer_1 (
    .in0(in_7), .in1(in_7), .in2(not_1_out), .in3(not_2_out), .in4(not_2_out), .in5(not_1_out),
    .in6(not_1_out), .in7(X), .out(multiplexer_1_out), .sel(in_9));
  Multiplexer #(.select(2)) multiplexer_2 (
    .in0(in_1), .in1(in_2), .in2(A), .in3(not_3_out), .out(multiplexer_2_out), .sel(BC));
  not not_3 (not_3_out, A);
  _74157 u_74157_1 (
    .pin1(in_5), .pin2(in_6), .pin3(n74157_1_pin3), .pin4(out_10));  // open: pin5, pin6, pin7, pin15, pin14, pin13, pin12, pin11, pin10, pin9
  LED led_1 (.in(multiplexer_1_out));
  LED led_2 (.in(multiplexer_2_out));
  not not_4 (n74157_1_pin3, in_6);

  // Notes on the sheet:
  //   4 * 1 MUX
  //   2 * 1 MUX for xor
endmodule
